// Logisim project 16-bit-ALU.circ as structural Verilog: 1 circuit, main circuit main
module main (
  input  [15:0] in_1,
  input  [15:0] in_2,
  input  [1:0] in_3,
  output [15:0] out_4
);

  wire undriven;
  wire [15:0] adder_1_out, and_1_out, or_1_out, xor_1_out;

  assign and_1_out = in_1 & and_1_out & in_1;  // AND_Gate and_1, 16 bits wide
  assign or_1_out = in_1 | in_2;  // OR_Gate or_1, 16 bits wide
  assign xor_1_out = in_1 ^ in_2;  // XOR_Gate xor_1, 16 bits wide
  Adder #(.width(16)) adder_1 (.a(in_1), .b(in_2), .out(adder_1_out));  // open: cin, cout
  Multiplexer #(.select(2), .width(16)) multiplexer_1 (
    .in0(and_1_out), .in1(or_1_out), .in2(xor_1_out), .in3(adder_1_out), .out(out_4), .sel(in_3),
    .en(undriven));
endmodule
